// Digital circuit BCD.dig as structural Verilog
module BCD (
  input  D,
  input  C,
  input  B,
  input  A
);

  wire _74247_1_pin9, _74247_1_pin10, _74247_1_pin11, _74247_1_pin12, _74247_1_pin13, _74247_1_pin14,
       _74247_1_pin15, u_kombnat_f;

  kombnat #(.applicationType("GHDL")) u_kombnat (.D(D), .C(C), .B(B), .A(A), .F(u_kombnat_f));
  _74247 _74247_1 (
    .pin1(B), .pin2(C), .pin3(1'b1), .pin4(u_kombnat_f), .pin5(1'b1), .pin6(D), .pin7(A), .pin8(1'b0),
    .pin9(_74247_1_pin9), .pin10(_74247_1_pin10), .pin11(_74247_1_pin11), .pin12(_74247_1_pin12),
    .pin13(_74247_1_pin13), .pin14(_74247_1_pin14), .pin15(_74247_1_pin15), .pin16(1'b1));
  Seven_Seg #(.commonCathode("true"), .commonConnectionType("anode")) seven_seg_1 (
    .a(_74247_1_pin13), .b(_74247_1_pin12), .c(_74247_1_pin11), .d(_74247_1_pin10), .e(_74247_1_pin9),
    .f(_74247_1_pin15), .g(_74247_1_pin14), .dp(1'b0), .common(1'b1));
endmodule

/* Code of kombnat:
library ieee;
use ieee.std_logic_1164.all;

entity kombnat is
  port (
      D,C,B,A : in std_logic;
      F : out std_logic
  );
end kombnat;

architecture behaviour of kombnat is
signal Cin, Cout : std_logic;
begin
  F <= (not D) or (not C and not B);
end architecture behaviour;
*/
