// Digital circuit JK_ff.dig as structural Verilog
module JK_ff (
  input  Cp
);

  wire A, B, nand_1_out, nand_2_out, nand_3_out, nand_4_out;
  wire [2:0] _7476_1_pin1;

  nand nand_1 (nand_1_out, A, B);
  nand nand_2 (nand_2_out, A, B);
  _7476 _7476_1 (
    .pin1(_7476_1_pin1[0]), .pin2(1'b1), .pin3(nand_1_out), .pin4(1'b1), .pin5(1'b1), .pin6(Cp), .pin7(1'b1),
    .pin8(nand_2_out), .pin9(1'b1), .pin10(_7476_1_pin1[0]), .pin11(_7476_1_pin1[0]), .pin12(1'b1),
    .pin13(1'b0), .pin15(B), .pin16(1'b1));  // open: pin14
  Seven_Seg_Hex seven_seg_hex_1 (.d({A, _7476_1_pin1[2], B, _7476_1_pin1[0]}), .dp(1'b0));
  LED V1 (.in(B));
  LED V0 (.in(_7476_1_pin1[0]));
  nand nand_3 (nand_3_out, A, B);
  nand nand_4 (nand_4_out, A, B);
  _7476 _7476_2 (
    .pin1(_7476_1_pin1[2]), .pin2(1'b1), .pin3(nand_3_out), .pin4(1'b1), .pin5(1'b1), .pin6(B), .pin7(1'b1),
    .pin8(nand_4_out), .pin9(1'b1), .pin10(_7476_1_pin1[2]), .pin11(_7476_1_pin1[2]), .pin12(1'b1),
    .pin13(1'b0), .pin15(A), .pin16(1'b1));  // open: pin14
  LED V3 (.in(A));
  LED V2 (.in(_7476_1_pin1[2]));
endmodule
