// Digital circuit ThreeBitCounter.dig as structural Verilog
module ThreeBitCounter (
  input  m0,
  input  m1,
  input  Clk,
  output q2,
  output q1,
  output q0
);

  ThreeBitCounter #(.applicationType("GHDL")) u_ThreeBitCounter (
    .Clk(Clk), .m1(m1), .m0(m0), .q2(q2), .q1(q1), .q0(q0));
  Seven_Seg_Hex seven_seg_hex_1 (.d({1'b0, q2, q1, q0}), .dp(1'b0));

  // Notes on the sheet:
  //   Clk: Hz: 2
endmodule

/* Code of ThreeBitCounter:
library ieee;
use ieee.std_logic_1164.all;
use ieee.numeric_std.all;

entity ThreeBitCounter is
    port (
        Clk        : in  std_logic;
        m1, m0     : in  std_logic;
        q2, q1, q0 : out std_logic
    );
end ThreeBitCounter;

architecture Behavioral of ThreeBitCounter is
    signal cnt : unsigned(2 downto 0) := "000";
    signal mode : std_logic_vector(1 downto 0);
begin
    -- Sammanfoga m1 och m0 signalerna till en 2-bitars logic vector signal
    mode <= m1 & m0;

    process(Clk)
    begin
        -- Vänta på klocksignal
        if rising_edge(Clk) then
            -- Beroende på läge i ingångarna m1 och m0
            case mode is
                -- m1m0 = 00 / aktuella tillståndet
                when "00" =>
                    q2 <= cnt(2);
                    q1 <= cnt(1);
                    q0 <= cnt(0);

                -- m1m0 = 01 / binär uppräkning
                when "01" =>
                    cnt <= cnt + 1;
                    q2 <= cnt(2);
                    q1 <= cnt(1);
                    q0 <= cnt(0);

                -- m1m0 = 10 / binär nedräkning
                when "10" =>
                    cnt <= cnt - 1;
                    q2 <= cnt(2);
                    q1 <= cnt(1);
                    q0 <= cnt(0);

                -- m1m0 = 11 / räkna med 2
                when "11" =>
                    cnt <= cnt + 2;
                    q2 <= cnt(2);
                    q1 <= cnt(1);
                    q0 <= cnt(0);

                -- Andra värden not expected, gör ingenting
                when others =>
                    null;
            end case;
        end if;
    end process;
end Behavioral;
*/
