// Digital circuit nineMinusX.dig as structural Verilog
module nineMinusX (
  input  x4,
  input  x3,
  input  x2,
  input  x1,
  output BCD,
  output u4,
  output u3,
  output u2,
  output u1
);

  wire nand_1_out, nand_2_out, nand_3_out, nand_4_out, nand_6_out, nand_7_out, nand_8_out, nand_9_out,
       nand_10_out, nand_11_out, nand_12_out, nand_13_out;

  nand nand_1 (nand_1_out, x2, x2);
  nand nand_2 (nand_2_out, x4, x4);
  nand nand_3 (nand_3_out, x3, x3);
  nand nand_4 (nand_4_out, x1, x1);
  nand nand_5 (BCD, x4, nand_6_out);
  nand nand_6 (nand_6_out, nand_1_out, nand_3_out);
  nand nand_7 (nand_7_out, nand_1_out, nand_1_out);
  nand nand_8 (nand_8_out, nand_7_out, nand_2_out);
  nand nand_9 (nand_9_out, nand_1_out, nand_2_out, nand_3_out);
  nand nand_10 (nand_10_out, nand_7_out, nand_2_out, nand_3_out);
  nand nand_11 (nand_11_out, x3, nand_1_out, nand_2_out);
  nand nand_12 (nand_12_out, nand_4_out, nand_2_out);
  nand nand_13 (nand_13_out, nand_4_out, nand_1_out, nand_3_out);
  nand nand_14 (u4, BCD, nand_9_out);
  nand nand_15 (u3, nand_10_out, BCD, nand_11_out);
  nand nand_16 (u2, nand_8_out, BCD);
  nand nand_17 (u1, nand_12_out, BCD, nand_13_out);
  Seven_Seg_Hex seven_seg_hex_1 (.d({u4, u3, u2, u1}), .dp(1'b0));
endmodule
